# Fritzing sketch piled3 (saved by Fritzing 0.9.3b)
circuit board: 4.49723cm x 5.07099cm
breadboards: 1

parts:
  ULN2003 = ULN2003A [package="DIP16 [THT]"]
  Test = Pushbutton [package="[THT]"]
  Power = female pin header, 2 pins [form="♀ (female)"]
  ULN2003_2 = ULN2003A [package="DIP16 [THT]"]
  Input = female pin header, 14 pins [form="♀ (female)"]
  Out = double row female pin header, 28 pins [form="♀ (female)"]

nets (from the pcb view):
  N1: ULN2003.In_1, Input.pin8
  N2: ULN2003.In_2, Input.pin9
  N3: ULN2003.In_3, Input.pin10
  N4: ULN2003.In_4, Input.pin11
  N5: ULN2003.In_5, Input.pin12
  N6: ULN2003.In_6, Input.pin13
  N7: ULN2003.In_7, Input.pin14
  N8: ULN2003.0V, Test.Pin_1, Test.Pin_2, Power.pin2, ULN2003_2.0V
  N9: ULN2003.COM_-_Common, Test.Pin_3, Test.Pin_4, ULN2003_2.COM_-_Common
  N10: ULN2003.Out_7, Out.pin14
  N11: ULN2003.Out_6, Out.pin13
  N12: ULN2003.Out_5, Out.pin12
  N13: ULN2003.Out_4, Out.pin11
  N14: ULN2003.Out_3, Out.pin10
  N15: ULN2003.Out_2, Out.pin9
  N16: ULN2003.Out_1, Out.pin8
  N17: Power.pin1, Out.pin15, Out.pin16, Out.pin17, Out.pin18, Out.pin19, Out.pin20, Out.pin21, Out.pin22, Out.pin23, Out.pin24, Out.pin25, Out.pin26, Out.pin27, Out.pin28
  N18: ULN2003_2.In_1, Input.pin1
  N19: ULN2003_2.In_2, Input.pin2
  N20: ULN2003_2.In_3, Input.pin3
  N21: ULN2003_2.In_4, Input.pin4
  N22: ULN2003_2.In_5, Input.pin5
  N23: ULN2003_2.In_6, Input.pin6
  N24: ULN2003_2.In_7, Input.pin7
  N25: ULN2003_2.Out_7, Out.pin7
  N26: ULN2003_2.Out_6, Out.pin6
  N27: ULN2003_2.Out_5, Out.pin5
  N28: ULN2003_2.Out_4, Out.pin4
  N29: ULN2003_2.Out_3, Out.pin3
  N30: ULN2003_2.Out_2, Out.pin2
  N31: ULN2003_2.Out_1, Out.pin1

notes:
  VCC
  GND
  Lamp Test
  I1
  I14
  O14
  O1
  v1 - Copyright 2018  @alanswx
  O7
  I8
  O8
  I7
